# Fritzing sketch UNO ExtremeExtreme (saved by Fritzing 0.9.3b)
circuit board: 5.6cm x 4.6cm
breadboards: 1

parts:
  Bauteil2 = Arduino Nano (Rev3.0)
  L293D = L293D [package=THT]
  Motor = female pin header, 2 pins [form="♀ (female)"]
  VIN = female pin header, 2 pins [form="♀ (female)"]
  SPK = female pin header, 2 pins [form="♀ (female)"]
  USB = female pin header, 4 pins [form="♀ (female)"]
  DFRobot_DFPlayer_Mini1 = DFRobot DFPlayer Mini [part_number=DFR0299]
  R1 = Resistor [tolerance=±5% resistance=1k package=THT]
  Btn = female pin header, 2 pins [form="♀ (female)"]
  Sfty = female pin header, 2 pins [form="♀ (female)"]
  Pad1 = Pad [width=2 height=2 connect=center]  # not connected
  RGB = female pin header, 3 pins [form="♀ (female)"]
  Btn1 = female pin header, 4 pins [form="♀ (female)"]

nets:
  N1: Bauteil2.GND, L293D.0V, VIN.pin2, USB.pin4, DFRobot_DFPlayer_Mini1.GND-1, DFRobot_DFPlayer_Mini1.GND-2, Btn.pin1, Sfty.pin1, RGB.pin1, Btn1.pin2
  N2: Bauteil2.D2, Btn.pin2
  N3: Bauteil2.D3, Sfty.pin2
  N4: Bauteil2.D4, RGB.pin2
  N5: Bauteil2.D5, DFRobot_DFPlayer_Mini1.TX
  N6: Bauteil2.D6, DFRobot_DFPlayer_Mini1.RX, R1.Pin_0, R1.Pin_1
  N7: Bauteil2.D7, DFRobot_DFPlayer_Mini1.BUSY
  N8: Bauteil2.D9, L293D.In_2
  N9: Bauteil2.D11/MOSI, L293D.Enable_1
  N10: Bauteil2.D12/MISO, L293D.In_1
  5V: Bauteil2.5V, L293D.+V, USB.pin1, DFRobot_DFPlayer_Mini1.VCC, RGB.pin3, Btn1.pin1
  N11: L293D.Out_1_(_Controlled_by_Enable_1_), Motor.pin2
  N12: L293D.Out_2_(_Controlled_by_Enable_1_), Motor.pin1
  N13: L293D.+Vmotor, VIN.pin1, Btn1.pin3, Btn1.pin4
  N14: SPK.pin1, DFRobot_DFPlayer_Mini1.SPK_1
  N15: SPK.pin2, DFRobot_DFPlayer_Mini1.SPK_2
  N16: USB.pin2, DFRobot_DFPlayer_Mini1.USB_NEG
  N17: USB.pin3, DFRobot_DFPlayer_Mini1.USB_POS
